# Fritzing sketch SunWaterControl (saved by Fritzing 0.9.3b)
circuit board: 8.46667cm x 5.64444cm
breadboards: 1

parts:
  ARDUINO_NANO = Arduino Nano (Rev3.0) (ICSP)
  ESP-01 = ESP8266 WiFi Module [part_number=ESP8266]
  USB_CONNECTOR = Mini-USB _B_ connector with 5th pin broken out. [package=usb-minib]
  REGULATOR_(5V->3_3V) = LD33 Low-Dropout Voltage Regulator
  U3 = L9110 H-bridge module [part_number="L9110 H-bridge"]
  J1_-_ESP_[GPIO2-GPIO0] = female pin header, 4 pins [form="♀ (female)"]
  J2_-_ESP_[TX-RX] = female pin header, 2 pins [form="♀ (female)"]
  J3 = female pin header, 1 pin [form="♀ (female)"]
  J4 = female pin header, 1 pin [form="♀ (female)"]
  J5_-_[D9/IA-A] = female pin header, 1 pin [form="♀ (female)"]
  J6_-_[D5/IA-B] = female pin header, 1 pin [form="♀ (female)"]
  J5_MOTOR = Screw terminal - 2 pins [package=THT]
  BH1750 = BH1750

nets:
  N1: ARDUINO_NANO.D1/TX, ESP-01.GPIO_0, J1_-_ESP_[GPIO2-GPIO0].pin1, J1_-_ESP_[GPIO2-GPIO0].pin2
  N2: ARDUINO_NANO.D0/RX, ESP-01.GPIO_2, J1_-_ESP_[GPIO2-GPIO0].pin3, J1_-_ESP_[GPIO2-GPIO0].pin4
  GND: ARDUINO_NANO.GND, ESP-01.GND, USB_CONNECTOR.GND, REGULATOR_(5V->3_3V).GND, U3.GND, BH1750.GND, BH1750.ADDR
  N3: ARDUINO_NANO.D5, U3.A-IB, J6_-_[D5/IA-B].pin1
  N4: ARDUINO_NANO.D9, U3.A-IA, J5_-_[D9/IA-A].pin1
  VIN: ARDUINO_NANO.VIN, USB_CONNECTOR.VBUS, REGULATOR_(5V->3_3V).Vin, U3.VCC
  N5: ARDUINO_NANO.A5, J3.pin1, BH1750.SCL
  N6: ARDUINO_NANO.A4, J4.pin1, BH1750.SDA
  N7: ESP-01.RXD, J2_-_ESP_[TX-RX].pin1
  N8: ESP-01.VCC, ESP-01.CH_PD
  N9: ESP-01.TXD, J2_-_ESP_[TX-RX].pin2
  N10: REGULATOR_(5V->3_3V).Vout, BH1750.VCC
  N11: U3.MOTOR_A-A, J5_MOTOR.pin1
  N12: U3.MOTOR_A-B, J5_MOTOR.pin2

custom parts:
  ESP8266 WiFi Module: Generic WiFi Module based on the ESP8266 with onboard PCB antenna and UART communications
  BH1750: Light Sensor
